// Digital circuit ejercicio_1a.dig as structural Verilog
module ejercicio_1a (
  input  A,
  input  B,
  input  C,
  output Z
);

  wire and_1_out, and_2_out, nand_1_out, nor_1_out, not_2_out, not_3_out, or_1_out, xor_1_out;

  // Not not_1 has open pins: in=A, out=open
  not not_2 (not_2_out, B);
  not not_3 (not_3_out, C);
  nor nor_1 (nor_1_out, A, not_2_out);
  xor xor_1 (xor_1_out, not_3_out, A);
  and and_1 (and_1_out, not_2_out, C);
  and and_2 (and_2_out, A, not_3_out);
  nand nand_1 (nand_1_out, nor_1_out, xor_1_out);
  or or_1 (or_1_out, and_1_out, and_2_out);
  nor nor_2 (Z, nand_1_out, or_1_out);
endmodule
