// Digital circuit ejercicio_1b.dig as structural Verilog
module ejercicio_1b (
  input  A,
  input  B,
  input  C,
  output Z
);

  wire not_1_out, not_2_out;

  not not_1 (not_1_out, A);
  not not_2 (not_2_out, C);
  and and_1 (Z, not_1_out, B, not_2_out);
endmodule
