// Digital circuit ejercicio_2.dig as structural Verilog
module ejercicio_2 (
  input  A,
  input  B,
  input  C
);

  wire and_1_out, nand_1_out, nand_2_out, nand_3_out, nand_4_out, nor_1_out, not_1_out, not_2_out, or_1_out,
       or_2_out;

  not not_1 (not_1_out, A);
  not not_2 (not_2_out, B);
  // Not not_3 has open pins: in=C, out=open
  nand nand_1 (nand_1_out, A, C);
  nand nand_2 (nand_2_out, A, B);
  or or_1 (or_1_out, not_2_out, C);
  nand nand_3 (nand_3_out, nand_1_out, not_2_out);
  and and_1 (and_1_out, not_1_out, C);
  nand nand_4 (nand_4_out, nand_2_out, or_1_out);
  nor nor_1 (nor_1_out, nand_3_out, and_1_out);
  or or_2 (or_2_out, nand_4_out, nor_1_out);
  LED Z (.in(or_2_out));
endmodule
