// Digital circuit ejercicio_2b.dig as structural Verilog
module ejercicio_2b (
  input  A,
  input  B,
  input  C
);

  wire and_1_out, not_3_out, or_1_out;

  // Not not_1 has open pins: in=A, out=open
  // Not not_2 has open pins: in=B, out=open
  not not_3 (not_3_out, C);
  and and_1 (and_1_out, B, A);
  or or_1 (or_1_out, not_3_out, and_1_out);
  LED Z (.in(or_1_out));
endmodule
